# Fritzing sketch simpleschema (saved by Fritzing 0.9.3b)
circuit board: 4.38721cm x 3.14407cm
breadboards: 1

parts:
  Componente1 = Arduino Uno (Rev3)
  C1 = Electrolytic Capacitor [capacitance=1µF package="100 mil [THT, electrolytic]"]
  IC1 = IC, DIP package, 16 pins [chip_label=IC]
  Voltage_microcontroller_in = female pin header, 2 pins [form="♀ (female)"]
  R1 = Resistor [tolerance=±5% resistance=220 package=THT]
  R2 = Resistor [tolerance=±5% resistance=220 package=THT]
  R3 = Photocell (LDR) [package=THT]
  R4 = Resistor [tolerance=±5% resistance=220 package=THT]
  J1 = female pin header, 1 pin [form="♀ (female)"]
  Tester_GND_Black = female pin header, 1 pin [form="♀ (female)"]

nets (from the breadboard view):
  N1: Componente1.A4/SDA, IC1.pin9, R2.Pin_0
  N2: Componente1.A5/SCL, IC1.pin10, R1.Pin_0
  N3: Componente1.5V, C1.+, IC1.pin14, IC1.pin16, Voltage_microcontroller_in.pin2, R1.Pin_1, R2.Pin_1
  N4: Componente1.GND, C1.-, IC1.pin12, IC1.pin13, Voltage_microcontroller_in.pin1, Tester_GND_Black.pin1
  N5: IC1.pin1, R3.pin_0, R4.Pin_1
  N6: IC1.pin2, R3.pin_1
  N7: IC1.pin3, IC1.pin4, IC1.pin5, IC1.pin6, IC1.pin7, IC1.pin8, R4.Pin_0
  N8: IC1.pin15, J1.pin1

notes:
  GND Black wire of tester
  Output red wire of tester
